# Fritzing sketch speedometer (saved by Fritzing 0.9.0b)
circuit board: 8.46667cm x 5.64444cm
breadboards: 1

parts:
  S1 = Reed switch [package=THT]
  S2 = Round Pushbutton
  Part2 = Arduino Micro (Rev3)
  VCC1 = Battery block 9V
  R1 = Resistor [package="0402 [SMD]"]
  U1 = Graphical LCD 128x64 [package=lcd-g12864]
  R3 = Rotary Potentiometer (Small) [package=THT]
  S3 = Round Pushbutton

nets:
  5V: S1.pin_1, Part2.5V, U1.VDD, U1.E, R3.leg1
  N1: S1.pin_2, R1.Pin_1
  N2: S2.leg0, Part2.GND
  N3: S2.leg1, VCC1.-, R1.Pin_0
  N4: Part2.D2/SDA, U1.CS2
  N5: Part2.D3/SCL, U1.DB7
  N6: Part2.D4_PWM/A6, U1.DB6
  N7: Part2.D5_PWM, U1.DB5
  N8: Part2.D11_PWM, U1.CS1
  N9: Part2.D12_PWM/A11, U1.D_I
  N10: Part2.VIN, VCC1.+
  N11: U1.RST, S3.leg0
  N12: U1.A, R3.leg2
  N13: U1.K, R3.wiper, S3.leg1

custom parts:
  Rotary Potentiometer (Small): A rotary adjustable resistor (potentiometer).
